# Fritzing sketch schematic_variation_1 (saved by Fritzing 0.9.4)
breadboards: 2

parts:
  Part1 = NeoPixel NeoMatrix 8x8 [part_number=1487]  # not connected
  J1 = Piezo Speaker
  S2 = Pushbutton [package="[THT]"]
  S4 = Pushbutton [package="[THT]"]
  Part2 = TFT 1.8 inch 160x128 w microSD [part_number=358]
  S5 = Pushbutton [package="[THT]"]
  S6 = Pushbutton [package="[THT]"]
  Mod1 = Raspberry Pi Pico
  S7 = Pushbutton [package="[THT]"]

nets:
  N1: J1.pin1, S2.Pin_3, S2.Pin_4, S4.Pin_3, S4.Pin_4, Part2.TFTDC, S6.Pin_3, S6.Pin_4, Mod1.pin_3, Mod1.pin_8, Mod1.pin_13, Mod1.pin_18, Mod1.pin_23, Mod1.pin_28, Mod1.pin_33, Mod1.pin_38, S7.Pin_1, S7.Pin_2
  N2: J1.pin2, Mod1.pin_7
  N3: S2.Pin_1, S2.Pin_2, Mod1.pin_27
  N4: S4.Pin_1, S4.Pin_2, Mod1.pin_26
  N5: Part2.LITE, Part2.RESET, Mod1.pin_40
  N6: Part2.MISO, Mod1.pin_4
  N7: Part2.SCLK, Mod1.pin_2
  N8: Part2.MOSI, Mod1.pin_1
  N9: Part2.TFTCS, Mod1.pin_5
  N10: Part2.CARDCS, Mod1.pin_6
  N11: S5.Pin_1, S5.Pin_2, Mod1.pin_20
  N12: S5.Pin_3, S5.Pin_4
  N13: S6.Pin_1, S6.Pin_2, Mod1.pin_10
  N14: Mod1.pin_30, S7.Pin_3, S7.Pin_4

custom parts:
  NeoPixel NeoMatrix 8x8: Put on your sunglasses before wiring up this LED matrix - 64 eye-blistering RGB LEDs adorn the NeoMatrix for a blast of configurable color. Arranged in an 8x8 matrix, each pixel is individually addressable. Only one microcontroller pin is required to control all the LEDs, and you get 24 bit color for each LED.
  TFT 1.8 inch 160x128 w microSD: This lovely little display breakout is the best way to add a small, colorful and bright display to any project. Since the display uses 4-wire SPI to communicate and has its own pixel-addressable frame buffer, it can be used with every kind of microcontroller. Even a very small one with low memory and few pins available! The 1.8" display has 128x160 color pixels.
  Raspberry Pi Pico: Raspberry Pi Pico. Based around the RP2040 microcontroller the Pico is a low cost microcontroller device bringing Raspberry Pi quality, cost, and easy of use to the microcontroller space. Jan 2021, fixed pcb so holes will be drilled for the pins. Added mounting holes to silkscreen (to drill mounting holes the user needs to drag a hole from core parts/pcb over the hole in silkscreen, by default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
